# Fritzing sketch Wiring (saved by Fritzing 1.0.3b)
breadboards: 1

parts:
  WS2812B_JST_Connector = mystery part, 3 pins [chip_label=?]
  Power_Switch = Square Pushbutton
  WS2812B_Additional_Power_Cables = mystery part, 2 pins [chip_label=?]
  ESP-32 = mystery part, 3 pins [chip_label=?]

nets:
  N1: WS2812B_JST_Connector.pin1, Power_Switch.leg0, WS2812B_Additional_Power_Cables.pin1
  N2: WS2812B_JST_Connector.pin2, WS2812B_Additional_Power_Cables.pin2, ESP-32.pin2
  N3: WS2812B_JST_Connector.pin3, ESP-32.pin3
  N4: Power_Switch.leg1, ESP-32.pin1
